# Fritzing sketch Arduino Dual LFO (saved by Fritzing 0.8.0b)
breadboards: 1

parts:
  Part1 = Arduino Uno (Rev3)
  R1 = Resistor [tolerance=±5% resistance=1k part_number="Lowpass (2)" package=THT]
  C1 = Ceramic Capacitor [capacitance=100nF package="100 mil [THT, multilayer]"]
  C2 = Ceramic Capacitor [capacitance=100nF package="100 mil [THT, multilayer]"]
  S5 = Round Pushbutton [part_number="Wave (1)"]
  LED2 = LED - 5mm [color="Red (633nm)" part_number=(0) package="5 mm [THT]"]
  R4 = Resistor [tolerance=±5% resistance=1k package=THT]
  R5 = Resistor [tolerance=±5% resistance=1k package=THT]
  S6 = Round Pushbutton [part_number="Wave (2)"]
  S7 = Round Pushbutton [part_number="Mode Switch"]
  R6 = Rotary Potentiometer (Small) [maximum_resistance=10kΩ part_number="Freq (1)"]
  R7 = Rotary Potentiometer (Small) [maximum_resistance=10kΩ part_number="Depth (1)"]
  R9 = Rotary Potentiometer (Small) [maximum_resistance=10kΩ part_number="Depth (2)"]
  R8 = Rotary Potentiometer (Small) [maximum_resistance=10kΩ part_number="Freq (2)"]
  LED3 = LED - 5mm [color="Red (633nm)" part_number=(1) package="5 mm [THT]"]
  R2 = Resistor [tolerance=±5% resistance=1k part_number="Lowpass (1)" package=THT]

nets:
  Frequency (1): Part1.A0, R6.wiper
  Frequency (2): Part1.A1, R8.wiper
  Depth (1): Part1.A4/SDA, R7.wiper
  Depth (2): Part1.A5/SCL, R9.wiper
  GND: Part1.GND, C1.1, C2.1, S5.leg1, R4.Pin_1, R5.Pin_1, S6.leg1, S7.leg1, R6.leg1, R7.leg1, R9.leg1, R8.leg1
  LED Bar 1: Part1.D8, LED3.anode
  Mode Switch: Part1.D9_PWM, S7.leg0
  Wave Switch (1): Part1.D10_PWM/SS, S5.leg0
  PWM (2): Part1.D11_PWM/MOSI, R1.Pin_0
  Wave Switch (2): Part1.D12/MISO, S6.leg0
  PWM (1): Part1.D3_PWM, R2.Pin_0
  LED Bar 0: Part1.D7, LED2.anode
  5V: Part1.5V, R7.leg2, R9.leg2
  LFO (2): R1.Pin_1, C1.0
  LFO (1): C2.0, R2.Pin_1
  N1: LED2.cathode, R4.Pin_0
  N2: R5.Pin_0, LED3.cathode

notes:
  LFO 1 & 2 OUT :
  MODE SWITCH
  LFO (1)
  WAVEFORM SELECTOR SWITCH
  FREQUENCY POT
  DEPT POT
  LFO (2)
  WAVEFORM SELECTOR SWITCH
  FREQUENCY POT
  DEPT POT
  LED BAR
